// Logisim project Tennis.circ as structural Verilog: 9 circuits, main circuit main
module main (
);

  wire clock_1_out;
  wire [4:0] joystick_1_y, kinematiccontroller_1_ballx, kinematiccontroller_1_bally,
       kinematiccontroller_1_chipid, kinematiccontroller_1_leftbaty, kinematiccontroller_1_rightbaty,
       not_1_out, undriven, videosection_1_ballx_2, videosection_1_bally_2, videosection_1_chipid_2,
       videosection_1_leftbaty_2, videosection_1_rightbaty_2, videosection_2_ballx_2, videosection_2_bally_2,
       videosection_2_chipid_2, videosection_2_leftbaty_2, videosection_2_rightbaty_2,
       videosection_3_ballx_2, videosection_3_bally_2, videosection_3_chipid_2, videosection_3_leftbaty_2,
       videosection_3_rightbaty_2;
  wire [7:0] kinematiccontroller_1_vxy, kinematiccontroller_1_xball, kinematiccontroller_1_yball, ls, rs;
  wire [31:0] videosection_1__0, videosection_1_out_7, videosection_1_out_8, videosection_1_out_9,
       videosection_1_out_10, videosection_1_out_11, videosection_1_out_12, videosection_1_out_13,
       videosection_2__0, videosection_2_out_7, videosection_2_out_8, videosection_2_out_9,
       videosection_2_out_10, videosection_2_out_11, videosection_2_out_12, videosection_2_out_13,
       videosection_3__0, videosection_3_out_7, videosection_3_out_8, videosection_3_out_9,
       videosection_3_out_10, videosection_3_out_11, videosection_3_out_12, videosection_3_out_13,
       videosection_4__0, videosection_4_out_7, videosection_4_out_8, videosection_4_out_9,
       videosection_4_out_10, videosection_4_out_11, videosection_4_out_12, videosection_4_out_13;

  Hex_Digit_Display hex_digit_display_1 ();  // open: value, dp
  Hex_Digit_Display hex_digit_display_2 ();  // open: value, dp
  Joystick #(.bits(5)) joystick_1 (.y(joystick_1_y));  // open: x
  // Probe on joystick_1_y
  assign not_1_out = ~joystick_1_y;  // NOT_Gate not_1, 5 bits wide
  // Probe on not_1_out
  DotMatrix #(.matrixcols(32), .matrixrows(32)) dotmatrix_1 (
    .col0(videosection_1__0), .col1(videosection_1_out_7), .col2(videosection_1_out_8),
    .col3(videosection_1_out_9), .col4(videosection_1_out_10), .col5(videosection_1_out_11),
    .col6(videosection_1_out_12), .col7(videosection_1_out_13), .col8(videosection_2__0),
    .col9(videosection_2_out_7), .col10(videosection_2_out_8), .col11(videosection_2_out_9),
    .col12(videosection_2_out_10), .col13(videosection_2_out_11), .col14(videosection_2_out_12),
    .col15(videosection_2_out_13), .col16(videosection_3__0), .col17(videosection_3_out_7),
    .col18(videosection_3_out_8), .col19(videosection_3_out_9), .col20(videosection_3_out_10),
    .col21(videosection_3_out_11), .col22(videosection_3_out_12), .col23(videosection_3_out_13),
    .col24(videosection_4__0), .col25(videosection_4_out_7), .col26(videosection_4_out_8),
    .col27(videosection_4_out_9), .col28(videosection_4_out_10), .col29(videosection_4_out_11),
    .col30(videosection_4_out_12), .col31(videosection_4_out_13));
  kinematicController kinematiccontroller_1 (
    .chipId(kinematiccontroller_1_chipid), .ballX(kinematiccontroller_1_ballx),
    .ballY(kinematiccontroller_1_bally), .leftBatY(kinematiccontroller_1_leftbaty),
    .rightBatY(kinematiccontroller_1_rightbaty), .Joystick(not_1_out), .Clock(clock_1_out),
    .rightBatPositionIn(undriven), .xball(kinematiccontroller_1_xball), .yball(kinematiccontroller_1_yball),
    .vxy(kinematiccontroller_1_vxy), .scoreA(ls), .scoreB(rs));
  videoSection videosection_1 (
    .chipId(kinematiccontroller_1_chipid), .ballX(kinematiccontroller_1_ballx),
    .ballY(kinematiccontroller_1_bally), .leftBatY(kinematiccontroller_1_leftbaty),
    .rightBatY(kinematiccontroller_1_rightbaty), .chipId_2(videosection_1_chipid_2),
    .ballX_2(videosection_1_ballx_2), .ballY_2(videosection_1_bally_2),
    .leftBatY_2(videosection_1_leftbaty_2), .rightBatY_2(videosection_1_rightbaty_2), ._0(videosection_1__0),
    .out_7(videosection_1_out_7), .out_8(videosection_1_out_8), .out_9(videosection_1_out_9),
    .out_10(videosection_1_out_10), .out_11(videosection_1_out_11), .out_12(videosection_1_out_12),
    .out_13(videosection_1_out_13));
  Clock clock_1 (.out(clock_1_out));
  videoSection videosection_2 (
    .chipId(videosection_1_chipid_2), .ballX(videosection_1_ballx_2), .ballY(videosection_1_bally_2),
    .leftBatY(videosection_1_leftbaty_2), .rightBatY(videosection_1_rightbaty_2),
    .chipId_2(videosection_2_chipid_2), .ballX_2(videosection_2_ballx_2), .ballY_2(videosection_2_bally_2),
    .leftBatY_2(videosection_2_leftbaty_2), .rightBatY_2(videosection_2_rightbaty_2), ._0(videosection_2__0),
    .out_7(videosection_2_out_7), .out_8(videosection_2_out_8), .out_9(videosection_2_out_9),
    .out_10(videosection_2_out_10), .out_11(videosection_2_out_11), .out_12(videosection_2_out_12),
    .out_13(videosection_2_out_13));
  videoSection videosection_3 (
    .chipId(videosection_2_chipid_2), .ballX(videosection_2_ballx_2), .ballY(videosection_2_bally_2),
    .leftBatY(videosection_2_leftbaty_2), .rightBatY(videosection_2_rightbaty_2),
    .chipId_2(videosection_3_chipid_2), .ballX_2(videosection_3_ballx_2), .ballY_2(videosection_3_bally_2),
    .leftBatY_2(videosection_3_leftbaty_2), .rightBatY_2(videosection_3_rightbaty_2), ._0(videosection_3__0),
    .out_7(videosection_3_out_7), .out_8(videosection_3_out_8), .out_9(videosection_3_out_9),
    .out_10(videosection_3_out_10), .out_11(videosection_3_out_11), .out_12(videosection_3_out_12),
    .out_13(videosection_3_out_13));
  videoSection videosection_4 (
    .chipId(videosection_3_chipid_2), .ballX(videosection_3_ballx_2), .ballY(videosection_3_bally_2),
    .leftBatY(videosection_3_leftbaty_2), .rightBatY(videosection_3_rightbaty_2), ._0(videosection_4__0),
    .out_7(videosection_4_out_7), .out_8(videosection_4_out_8), .out_9(videosection_4_out_9),
    .out_10(videosection_4_out_10), .out_11(videosection_4_out_11), .out_12(videosection_4_out_12),
    .out_13(videosection_4_out_13));  // open: chipId_2, ballX_2, ballY_2, leftBatY_2, rightBatY_2
  Hex_Digit_Display hex_digit_display_3 ();  // open: value, dp
  Hex_Digit_Display hex_digit_display_4 ();  // open: value, dp
endmodule

module VideoChip (
  input  [4:0] chipId,
  input  [4:0] ballX,
  input  [4:0] ballY,
  input  [4:0] leftBatY,
  input  [4:0] rightBatY,
  output [31:0] bitPattern,
  output [4:0] chipId_2,
  output [4:0] ballX_2,
  output [4:0] ballY_2,
  output [4:0] leftBatY_2,
  output [4:0] rightBatY_2
);

  wire comparator_1_eq, comparator_2_eq, comparator_3_eq, or_1_out;
  wire [31:0] ballvideo_1_out, chip_1_out_2, rightBatY_t;

  chip chip_1 (.in_1(leftBatY), .out_2(chip_1_out_2));
  Comparator #(.width(5), .mode("unsigned")) comparator_1 (
    .a(chipId), .b(5'b00011), .eq(comparator_1_eq));  // open: gt, lt
  Comparator #(.width(5), .mode("unsigned")) comparator_2 (
    .a(chipId), .b(5'b11100), .eq(comparator_2_eq));  // open: gt, lt
  Comparator #(.width(5), .mode("unsigned")) comparator_3 (
    .a(chipId), .b(ballX), .eq(comparator_3_eq));  // open: gt, lt
  ballVideo ballvideo_1 (.in(ballY), .out(ballvideo_1_out));
  Multiplexer #(.width(32)) multiplexer_1 (
    .in1(chip_1_out_2), .out(bitPattern), .sel(comparator_1_eq));  // open: in0, en
  or or_1 (or_1_out, comparator_1_eq, comparator_2_eq, comparator_3_eq);
  Multiplexer #(.width(32)) multiplexer_2 (
    .in1(ballvideo_1_out), .out(bitPattern), .sel(comparator_3_eq));  // open: in0, en
  chip chip_2 (.in_1(rightBatY), .out_2(rightBatY_t));
  Multiplexer #(.width(32)) multiplexer_3 (.in0({32{1'b0}}), .out(bitPattern), .sel(or_1_out));  // open: in1, en
  Multiplexer #(.width(32)) multiplexer_4 (
    .in1(rightBatY_t), .out(bitPattern), .sel(comparator_2_eq));  // open: in0, en
  inc inc_1 (.X(chipId), .R(chipId_2));  // open: Cout

  assign ballX_2 = ballX;
  assign ballY_2 = ballY;
  assign leftBatY_2 = leftBatY;
  assign rightBatY_2 = rightBatY;
endmodule

module videoSection (
  input  [4:0] chipId,
  input  [4:0] ballX,
  input  [4:0] ballY,
  input  [4:0] leftBatY,
  input  [4:0] rightBatY,
  output [31:0] _0,
  output [31:0] out_7,
  output [31:0] out_8,
  output [31:0] out_9,
  output [31:0] out_10,
  output [31:0] out_11,
  output [31:0] out_12,
  output [31:0] out_13,
  output [4:0] chipId_2,
  output [4:0] ballX_2,
  output [4:0] ballY_2,
  output [4:0] leftBatY_2,
  output [4:0] rightBatY_2
);

  wire [4:0] videochip_1_ballx_2, videochip_1_bally_2, videochip_1_chipid_2, videochip_1_leftbaty_2,
       videochip_1_rightbaty_2, videochip_2_ballx_2, videochip_2_bally_2, videochip_2_chipid_2,
       videochip_2_leftbaty_2, videochip_2_rightbaty_2, videochip_3_ballx_2, videochip_3_bally_2,
       videochip_3_chipid_2, videochip_3_leftbaty_2, videochip_3_rightbaty_2, videochip_4_ballx_2,
       videochip_4_bally_2, videochip_4_chipid_2, videochip_4_leftbaty_2, videochip_4_rightbaty_2,
       videochip_5_ballx_2, videochip_5_bally_2, videochip_5_chipid_2, videochip_5_leftbaty_2,
       videochip_5_rightbaty_2, videochip_6_ballx_2, videochip_6_bally_2, videochip_6_chipid_2,
       videochip_6_leftbaty_2, videochip_6_rightbaty_2, videochip_7_ballx_2, videochip_7_bally_2,
       videochip_7_chipid_2, videochip_7_leftbaty_2, videochip_7_rightbaty_2;

  VideoChip videochip_1 (
    .chipId(chipId), .ballX(ballX), .ballY(ballY), .leftBatY(leftBatY), .rightBatY(rightBatY),
    .bitPattern(_0), .chipId_2(videochip_1_chipid_2), .ballX_2(videochip_1_ballx_2),
    .ballY_2(videochip_1_bally_2), .leftBatY_2(videochip_1_leftbaty_2), .rightBatY_2(videochip_1_rightbaty_2));
  VideoChip videochip_2 (
    .chipId(videochip_3_chipid_2), .ballX(videochip_3_ballx_2), .ballY(videochip_3_bally_2),
    .leftBatY(videochip_3_leftbaty_2), .rightBatY(videochip_3_rightbaty_2), .bitPattern(out_8),
    .chipId_2(videochip_2_chipid_2), .ballX_2(videochip_2_ballx_2), .ballY_2(videochip_2_bally_2),
    .leftBatY_2(videochip_2_leftbaty_2), .rightBatY_2(videochip_2_rightbaty_2));
  VideoChip videochip_3 (
    .chipId(videochip_1_chipid_2), .ballX(videochip_1_ballx_2), .ballY(videochip_1_bally_2),
    .leftBatY(videochip_1_leftbaty_2), .rightBatY(videochip_1_rightbaty_2), .bitPattern(out_7),
    .chipId_2(videochip_3_chipid_2), .ballX_2(videochip_3_ballx_2), .ballY_2(videochip_3_bally_2),
    .leftBatY_2(videochip_3_leftbaty_2), .rightBatY_2(videochip_3_rightbaty_2));
  VideoChip videochip_4 (
    .chipId(videochip_5_chipid_2), .ballX(videochip_5_ballx_2), .ballY(videochip_5_bally_2),
    .leftBatY(videochip_5_leftbaty_2), .rightBatY(videochip_5_rightbaty_2), .bitPattern(out_11),
    .chipId_2(videochip_4_chipid_2), .ballX_2(videochip_4_ballx_2), .ballY_2(videochip_4_bally_2),
    .leftBatY_2(videochip_4_leftbaty_2), .rightBatY_2(videochip_4_rightbaty_2));
  VideoChip videochip_5 (
    .chipId(videochip_6_chipid_2), .ballX(videochip_6_ballx_2), .ballY(videochip_6_bally_2),
    .leftBatY(videochip_6_leftbaty_2), .rightBatY(videochip_6_rightbaty_2), .bitPattern(out_10),
    .chipId_2(videochip_5_chipid_2), .ballX_2(videochip_5_ballx_2), .ballY_2(videochip_5_bally_2),
    .leftBatY_2(videochip_5_leftbaty_2), .rightBatY_2(videochip_5_rightbaty_2));
  VideoChip videochip_6 (
    .chipId(videochip_2_chipid_2), .ballX(videochip_2_ballx_2), .ballY(videochip_2_bally_2),
    .leftBatY(videochip_2_leftbaty_2), .rightBatY(videochip_2_rightbaty_2), .bitPattern(out_9),
    .chipId_2(videochip_6_chipid_2), .ballX_2(videochip_6_ballx_2), .ballY_2(videochip_6_bally_2),
    .leftBatY_2(videochip_6_leftbaty_2), .rightBatY_2(videochip_6_rightbaty_2));
  VideoChip videochip_7 (
    .chipId(videochip_4_chipid_2), .ballX(videochip_4_ballx_2), .ballY(videochip_4_bally_2),
    .leftBatY(videochip_4_leftbaty_2), .rightBatY(videochip_4_rightbaty_2), .bitPattern(out_12),
    .chipId_2(videochip_7_chipid_2), .ballX_2(videochip_7_ballx_2), .ballY_2(videochip_7_bally_2),
    .leftBatY_2(videochip_7_leftbaty_2), .rightBatY_2(videochip_7_rightbaty_2));
  VideoChip videochip_8 (
    .chipId(videochip_7_chipid_2), .ballX(videochip_7_ballx_2), .ballY(videochip_7_bally_2),
    .leftBatY(videochip_7_leftbaty_2), .rightBatY(videochip_7_rightbaty_2), .bitPattern(out_13),
    .chipId_2(chipId_2), .ballX_2(ballX_2), .ballY_2(ballY_2), .leftBatY_2(leftBatY_2),
    .rightBatY_2(rightBatY_2));
endmodule

module kinematicController (
  input  [4:0] Joystick,
  input  [4:0] rightBatPositionIn,
  input  Clock,
  output [7:0] xball,
  output [4:0] chipId,
  output [7:0] yball,
  output [4:0] ballX,
  output [4:0] ballY,
  output [7:0] scoreA,
  output [7:0] scoreB,
  output [4:0] leftBatY,
  output [4:0] rightBatY,
  output [7:0] vxy
);

  wire adder_1_cout, adder_2_cout, adder_5_cout, adder_6_cout, and_1_out, and_2_out, comparator_1_lt,
       comparator_2_eq, comparator_3_eq, comparator_4_eq, comparator_5_eq, comparator_6_eq, comparator_7_eq,
       inrange_1_showarow, inrange_2_showarow, not_1_out, not_2_out, not_3_out, not_4_out, or_1_out,
       or_2_out, or_3_out;
  wire [2:0] ballX_q, ballY_q;
  wire [7:0] adder_3_out, adder_4_out, undriven;

  Register #(.width(3)) componentX (.Q(vxy[2:0]));  // open: D, en, clk, clr
  Register #(.width(3)) componentY (.Q(vxy[5:3]));  // open: D, en, clk, clr
  Register u_ballY (.Q({ballY, ballY_q}));  // open: D, en, clk, clr
  Register u_ballX (.D(undriven), .Q({ballX, ballX_q}));  // open: en, clk, clr
  Comparator #(.width(5), .mode("unsigned")) comparator_1 (
    .a({ballX[1:0], ballX_q}), .b(5'b01110), .lt(comparator_1_lt));  // open: gt, eq
  Adder adder_1 (.a({ballX, ballX_q}), .b({{6{vxy[2]}}, vxy[1:0]}), .cout(adder_1_cout));  // open: out, cin
  Comparator #(.width(1)) comparator_2 (.a(vxy[2]), .b(1'b1), .eq(comparator_2_eq));  // open: gt, lt
  Comparator #(.width(1)) comparator_3 (.a(vxy[5]), .b(1'b1), .eq(comparator_3_eq));  // open: gt, lt
  Register #(.width(5)) rightBatPosition (
    .D(rightBatPositionIn), .en(comparator_1_lt), .Q(rightBatY));  // open: clk, clr
  Comparator #(.width(1)) comparator_4 (.a(adder_1_cout), .b(comparator_2_eq), .eq(comparator_4_eq));  // open: gt, lt
  not not_1 (not_1_out, comparator_4_eq);
  Adder adder_2 (.a({ballY, ballY_q}), .b({{6{vxy[5]}}, vxy[4:3]}), .cout(adder_2_cout));  // open: out, cin
  Comparator #(.width(1)) comparator_5 (.a(adder_2_cout), .b(comparator_3_eq), .eq(comparator_5_eq));  // open: gt, lt
  Adder adder_3 (.a({ballX, ballX_q}), .b(8'he4), .out(adder_3_out));  // open: cin, cout
  or or_1 (or_1_out, not_1_out, vxy[2]);
  Adder adder_4 (.a({ballX, ballX_q}), .b(8'h1c), .out(adder_4_out));  // open: cin, cout
  or or_2 (or_2_out, vxy[5], not_2_out);
  not not_2 (not_2_out, comparator_5_eq);
  Adder adder_5 (.a(adder_3_out), .b({{6{vxy[2]}}, vxy[1:0]}), .cout(adder_5_cout));  // open: out, cin
  Adder adder_6 (.a(adder_4_out), .b({{6{vxy[2]}}, vxy[1:0]}), .cout(adder_6_cout));  // open: out, cin
  inrange inrange_1 (.Yball(ballY), .Ybat(Joystick), .ShowArow(inrange_1_showarow));
  not not_3 (not_3_out, comparator_6_eq);
  Comparator #(.width(1)) comparator_6 (.a(adder_5_cout), .b(comparator_2_eq), .eq(comparator_6_eq));  // open: gt, lt
  inrange inrange_2 (.Yball(ballY), .Ybat(rightBatY), .ShowArow(inrange_2_showarow));
  not not_4 (not_4_out, comparator_7_eq);
  Comparator #(.width(1)) comparator_7 (.a(adder_6_cout), .b(comparator_2_eq), .eq(comparator_7_eq));  // open: gt, lt
  and and_1 (and_1_out, inrange_1_showarow, not_3_out);
  and and_2 (and_2_out, inrange_2_showarow, not_4_out);
  or or_3 (or_3_out, and_1_out, and_2_out);
  Counter scoreLeft ();  // open: load, D, count, Q, carry, clk, clr
  Register ballY_2 ();  // open: D, en, Q, clk, clr
  Counter scoreRight ();  // open: load, D, count, Q, carry, clk, clr

  assign chipId = {5{1'b0}};
  assign leftBatY = Joystick;
  assign vxy[7:6] = 2'b00;

  // Notes on the sheet:
  //   hitB
  //   hitA
  //   LBcontact
  //   RBcontact
  //   BContact
endmodule

module inc (
  input  [4:0] X,
  output [4:0] R,
  output Cout
);

  wire [4:1] and_1_out;

  assign {Cout, and_1_out} = {and_1_out, 1'b1} & X;  // AND_Gate and_1, 5 bits wide
  assign R = X ^ {and_1_out, 1'b1};  // XOR_Gate xor_1, 5 bits wide
endmodule

module ballVideo (
  input  [4:0] in,
  output [31:0] out
);

  Shifter #(.width(32), .shift("rl")) shifter_1 (.in(32'h1), .\dist (in), .out(out));
endmodule

module chip (
  input  [4:0] in_1,
  output [31:0] out_2
);

  wire comparator_1_eq;
  wire [4:0] subtractor_1_out;
  wire [31:0] shifter_1_out, shifter_2_out;

  Comparator #(.width(5), .mode("unsigned")) comparator_1 (
    .a(in_1), .b(5'b11110), .eq(comparator_1_eq));  // open: gt, lt
  Shifter #(.width(32)) shifter_1 (.in(32'h7), .\dist (in_1), .out(shifter_1_out));
  Subtractor #(.width(5)) subtractor_1 (.a(in_1), .b(5'b00001), .out(subtractor_1_out));  // open: bin, bout
  Shifter #(.width(32)) shifter_2 (.in(32'h7), .\dist (subtractor_1_out), .out(shifter_2_out));
  Multiplexer #(.width(32)) multiplexer_1 (
    .in0(shifter_1_out), .in1(shifter_2_out), .out(out_2), .sel(comparator_1_eq));  // open: en
endmodule

module reflect (
  input  [2:0] \input ,
  output [2:0] \output 
);

  wire comparator_1_eq;
  wire [2:0] adder_1_out;

  Adder #(.width(3)) adder_1 (.a(\input ), .b(3'b001), .out(adder_1_out));  // open: cin, cout
  Multiplexer #(.width(3)) multiplexer_1 (
    .in0(adder_1_out), .in1(\input ), .out(\output ), .sel(comparator_1_eq));  // open: en
  Comparator #(.width(3), .mode("unsigned")) comparator_1 (
    .a(\input ), .b(3'b100), .eq(comparator_1_eq));  // open: gt, lt
endmodule

module inrange (
  input  [4:0] Yball,
  input  [4:0] Ybat,
  output ShowArow
);

  wire comparator_1_eq, comparator_2_eq, comparator_3_eq;
  wire [4:0] adder_1_out, inc_1_r;

  Comparator #(.width(5), .mode("unsigned")) comparator_1 (
    .a(Yball), .b(adder_1_out), .eq(comparator_1_eq));  // open: gt, lt
  Adder #(.width(5)) adder_1 (.a(Ybat), .b(5'b00010), .out(adder_1_out));  // open: cin, cout
  Comparator #(.width(5), .mode("unsigned")) comparator_2 (.a(Yball), .b(Ybat), .eq(comparator_2_eq));  // open: gt, lt
  Comparator #(.width(5), .mode("unsigned")) comparator_3 (
    .a(Yball), .b(inc_1_r), .eq(comparator_3_eq));  // open: gt, lt
  inc inc_1 (.X(Ybat), .R(inc_1_r));  // open: Cout
  or or_1 (ShowArow, comparator_1_eq, comparator_2_eq, comparator_3_eq);
endmodule
